// Logisim project p01-1.circ as structural Verilog: 3 circuits, main circuit main
module main (
  input  [7:0] in_1,
  input  [3:0] in_2,
  output [10:0] out_3
);

  wire [3:0] \continue , shifter_1_out, shifter_2_out, shifter_3_out, shifter_4_out, shifter_5_out,
       shifter_6_out, shifter_7_out, \除_1_out_3 , \除_2_out_3 , \除_3_out_3 , \除_4_out_3 , \除_6_out_3 ,
       \除_7_out_3 ;
  wire [3:3] \除_5_out_3 ;

  \除  \u_除_1  (.in_1(in_1[7:4]), .in_2(in_2), .out_3(\除_1_out_3 ));
  Shifter #(.width(4)) shifter_1 (.in(\除_1_out_3 ), .\dist (2'b01), .out(shifter_1_out));
  Shifter #(.width(4)) shifter_2 (.in(\continue ), .\dist (2'b01), .out(shifter_2_out));
  \除  \u_除_2  (.in_1({shifter_1_out[3:1], in_1[3]}), .in_2(in_2), .out_3(\除_2_out_3 ));
  Shifter #(.width(4)) shifter_3 (.in(\除_2_out_3 ), .\dist (2'b01), .out(shifter_3_out));
  \除  \u_除_3  (.in_1({shifter_2_out[3:1], 1'b0}), .in_2(in_2), .out_3(\除_3_out_3 ));
  Shifter #(.width(4)) shifter_4 (.in(\除_3_out_3 ), .\dist (2'b01), .out(shifter_4_out));
  \除  \u_除_4  (.in_1({shifter_3_out[3:1], in_1[2]}), .in_2(in_2), .out_3(\除_4_out_3 ));
  Shifter #(.width(4)) shifter_5 (.in(\除_4_out_3 ), .\dist (2'b01), .out(shifter_5_out));
  \除  \u_除_5  (.in_1({shifter_4_out[3:1], 1'b0}), .in_2(in_2), .out_3({\除_5_out_3 [3], out_3[2:0]}));
  \除  \u_除_6  (.in_1({shifter_5_out[3:1], in_1[1]}), .in_2(in_2), .out_3(\除_6_out_3 ));
  Shifter #(.width(4)) shifter_6 (.in(\除_6_out_3 ), .\dist (2'b01), .out(shifter_6_out));
  \除  \u_除_7  (.in_1({shifter_6_out[3:1], in_1[0]}), .in_2(in_2), .out_3(\除_7_out_3 ));
  Shifter #(.width(4)) shifter_7 (.in(\除_7_out_3 ), .\dist (2'b01), .out(shifter_7_out));
  \除  \u_除_8  (.in_1({shifter_7_out[3:1], 1'b0}), .in_2(in_2), .out_3(\continue ));

  assign out_3[10:3] = in_1;

  // Other names for the same wires on the sheet: _2 = in_1[2]; add[2:0] = out_3[2:0]; _3 = in_1[1]; _4 = in_1[0];
  //   in[3:0] = in_2; _1 = in_1[3]
endmodule

module \除  (
  input  [3:0] in_1,
  input  [3:0] in_2,
  output [3:0] out_3
);

  wire and_1_out;
  wire [3:0] xor_1_out;

  assign xor_1_out = in_1 ^ in_2;  // XOR_Gate xor_1, 4 bits wide
  and and_1 (and_1_out, 1'b1, in_1[3]);
  Multiplexer #(.width(4)) multiplexer_1 (.in0(in_1), .in1(xor_1_out), .out(out_3), .sel(and_1_out));  // open: en
endmodule

module CRC (
  input  [7:0] in_1,
  input  [3:0] in_2,
  output [10:0] out_3
);

  wire [3:0] \continue , shifter_1_out, shifter_2_out, shifter_3_out, shifter_4_out, shifter_5_out,
       shifter_6_out, shifter_7_out, \除_1_out_3 , \除_2_out_3 , \除_3_out_3 , \除_4_out_3 , \除_6_out_3 ,
       \除_7_out_3 ;
  wire [3:3] \除_5_out_3 ;

  \除  \u_除_1  (.in_1(in_1[7:4]), .in_2(in_2), .out_3(\除_1_out_3 ));
  Shifter #(.width(4)) shifter_1 (.in(\除_1_out_3 ), .\dist (2'b01), .out(shifter_1_out));
  Shifter #(.width(4)) shifter_2 (.in(\continue ), .\dist (2'b01), .out(shifter_2_out));
  \除  \u_除_2  (.in_1({shifter_1_out[3:1], in_1[3]}), .in_2(in_2), .out_3(\除_2_out_3 ));
  Shifter #(.width(4)) shifter_3 (.in(\除_2_out_3 ), .\dist (2'b01), .out(shifter_3_out));
  \除  \u_除_3  (.in_1({shifter_2_out[3:1], 1'b0}), .in_2(in_2), .out_3(\除_3_out_3 ));
  Shifter #(.width(4)) shifter_4 (.in(\除_3_out_3 ), .\dist (2'b01), .out(shifter_4_out));
  \除  \u_除_4  (.in_1({shifter_3_out[3:1], in_1[2]}), .in_2(in_2), .out_3(\除_4_out_3 ));
  Shifter #(.width(4)) shifter_5 (.in(\除_4_out_3 ), .\dist (2'b01), .out(shifter_5_out));
  \除  \u_除_5  (.in_1({shifter_4_out[3:1], 1'b0}), .in_2(in_2), .out_3({\除_5_out_3 [3], out_3[2:0]}));
  \除  \u_除_6  (.in_1({shifter_5_out[3:1], in_1[1]}), .in_2(in_2), .out_3(\除_6_out_3 ));
  Shifter #(.width(4)) shifter_6 (.in(\除_6_out_3 ), .\dist (2'b01), .out(shifter_6_out));
  \除  \u_除_7  (.in_1({shifter_6_out[3:1], in_1[0]}), .in_2(in_2), .out_3(\除_7_out_3 ));
  Shifter #(.width(4)) shifter_7 (.in(\除_7_out_3 ), .\dist (2'b01), .out(shifter_7_out));
  \除  \u_除_8  (.in_1({shifter_7_out[3:1], 1'b0}), .in_2(in_2), .out_3(\continue ));

  assign out_3[10:3] = in_1;

  // Other names for the same wires on the sheet: _2 = in_1[2]; add[2:0] = out_3[2:0]; _3 = in_1[1]; _4 = in_1[0];
  //   in[3:0] = in_2; _1 = in_1[3]
endmodule
