// Logisim project p01-2.circ as structural Verilog: 2 circuits, main circuit main
module main (
);

  Register #(.width(32)) register_1 ();  // open: D, en, Q, clk, clr
  Register #(.width(32)) register_2 ();  // open: D, en, Q, clk, clr
endmodule

// in18
module grf (
  input  clk,
  input  reset,
  input  [31:0] in_3,
  input  in_4,
  input  [4:0] in_5,
  input  [4:0] in_6,
  input  [4:0] in_7,
  output [31:0] out_8,
  output [31:0] out_9
);

  wire [31:0] in2, in3, in4, in5, in6, in7, in8, in9, in10, in11, in12, in13, in14, in15, in16, in17, in18,
       in19, in20, in21, in22, in23, in24, in25, in26, in27, in28, in29, in30, in31, in32, out2, out3, out4,
       out5, out6, out7, out8, out9, out10, out11, out12, out13, out14, out15, out16, out17, out18, out19,
       out20, out21, out22, out23, out24, out25, out26, out27, out28, out29, out30, out31, out32;

  Register #(.width(32)) register_1 (.clk(clk), .clr(reset));  // open: D, en, Q
  Register #(.width(32)) register_2 (.D(in11), .Q(out11), .clk(clk), .clr(reset));  // open: en
  Register #(.width(32)) register_3 (.D(in21), .Q(out21), .clk(clk), .clr(reset));  // open: en
  Register #(.width(32)) register_4 (.D(in31), .Q(out31), .clk(clk), .clr(reset));  // open: en
  Register #(.width(32)) register_5 (.D(in2), .Q(out2), .clk(clk), .clr(reset));  // open: en
  Register #(.width(32)) register_6 (.D(in12), .Q(out12), .clk(clk), .clr(reset));  // open: en
  Register #(.width(32)) register_7 (.D(in22), .Q(out22), .clk(clk), .clr(reset));  // open: en
  Register #(.width(32)) register_8 (.D(in32), .Q(out32), .clk(clk), .clr(reset));  // open: en
  Register #(.width(32)) register_9 (.D(in3), .Q(out3), .clk(clk), .clr(reset));  // open: en
  Register #(.width(32)) register_10 (.D(in13), .Q(out13), .clk(clk), .clr(reset));  // open: en
  Register #(.width(32)) register_11 (.D(in23), .Q(out23), .clk(clk), .clr(reset));  // open: en
  Multiplexer #(.select(5), .width(32), .enable("false")) multiplexer_1 (
    .in0({32{1'b0}}), .in1(out2), .in2(out3), .in3(out4), .in4(out5), .in5(out6), .in6(out7), .in7(out8),
    .in8(out9), .in9(out10), .in10(out11), .in11(out12), .in12(out13), .in13(out14), .in14(out15),
    .in15(out16), .in16(out17), .in17(out18), .in18(out19), .in19(out20), .in20(out21), .in21(out22),
    .in22(out23), .in23(out24), .in24(out25), .in25(out26), .in26(out27), .in27(out28), .in28(out29),
    .in29(out30), .in30(out31), .in31(out32), .out(out_9), .sel(in_7));
  Register #(.width(32)) register_12 (.D(in4), .Q(out4), .clk(clk), .clr(reset));  // open: en
  Register #(.width(32)) register_13 (.D(in14), .Q(out14), .clk(clk), .clr(reset));  // open: en
  Register #(.width(32)) register_14 (.D(in24), .Q(out24), .clk(clk), .clr(reset));  // open: en
  Register #(.width(32)) register_15 (.D(in5), .Q(out5), .clk(clk), .clr(reset));  // open: en
  Register #(.width(32)) register_16 (.D(in15), .Q(out15), .clk(clk), .clr(reset));  // open: en
  Register #(.width(32)) register_17 (.D(in25), .Q(out25), .clk(clk), .clr(reset));  // open: en
  Register #(.width(32)) register_18 (.D(in6), .Q(out6), .clk(clk), .clr(reset));  // open: en
  Register #(.width(32)) register_19 (.D(in16), .Q(out16), .clk(clk), .clr(reset));  // open: en
  Register #(.width(32)) register_20 (.D(in26), .Q(out26), .clk(clk), .clr(reset));  // open: en
  Multiplexer #(.select(5), .width(32), .enable("false")) multiplexer_2 (
    .in0({32{1'b0}}), .in1(out2), .in2(out3), .in3(out4), .in4(out5), .in5(out6), .in6(out7), .in7(out8),
    .in8(out9), .in9(out10), .in10(out11), .in11(out12), .in12(out13), .in13(out14), .in14(out15),
    .in15(out16), .in16(out17), .in17(out18), .in18(out19), .in19(out20), .in20(out21), .in21(out22),
    .in22(out23), .in23(out24), .in24(out25), .in25(out26), .in26(out27), .in27(out28), .in28(out29),
    .in29(out30), .in30(out31), .in31(out32), .out(out_8), .sel(in_6));
  Register #(.width(32)) register_21 (.D(in7), .Q(out7), .clk(clk), .clr(reset));  // open: en
  Register #(.width(32)) register_22 (.D(in17), .Q(out17), .clk(clk), .clr(reset));  // open: en
  Register #(.width(32)) register_23 (.D(in27), .Q(out27), .clk(clk), .clr(reset));  // open: en
  Register #(.width(32)) register_24 (.D(in8), .Q(out8), .clk(clk), .clr(reset));  // open: en
  Register #(.width(32)) register_25 (.D(in18), .Q(out18), .clk(clk), .clr(reset));  // open: en
  Register #(.width(32)) register_26 (.D(in28), .Q(out28), .clk(clk), .clr(reset));  // open: en
  Demultiplexer #(.select(5), .width(32), .tristate("true")) demultiplexer_1 (
    .out1(in2), .out2(in3), .out3(in4), .out4(in5), .out5(in6), .out6(in7), .out7(in8), .out8(in9),
    .out9(in10), .out10(in11), .out11(in12), .out12(in13), .out13(in14), .out14(in15), .out15(in16),
    .out16(in17), .out17(in18), .out18(in19), .out19(in20), .out20(in21), .out21(in22), .out22(in23),
    .out23(in24), .out24(in25), .out25(in26), .out26(in27), .out27(in28), .out28(in29), .out29(in30),
    .out30(in31), .out31(in32), .in(in_3), .sel(in_5), .en(in_4));  // open: out0
  Register #(.width(32)) register_27 (.D(in9), .Q(out9), .clk(clk), .clr(reset));  // open: en
  Register #(.width(32)) register_28 (.D(in19), .Q(out19), .clk(clk), .clr(reset));  // open: en
  Register #(.width(32)) register_29 (.D(in29), .Q(out29), .clk(clk), .clr(reset));  // open: en
  Register #(.width(32)) register_30 (.D(in10), .Q(out10), .clk(clk), .clr(reset));  // open: en
  Register #(.width(32)) register_31 (.D(in20), .Q(out20), .clk(clk), .clr(reset));  // open: en
  Register #(.width(32)) register_32 (.D(in30), .Q(out30), .clk(clk), .clr(reset));  // open: en

  // Other names for the same wires on the sheet: clear = reset
endmodule
