// Logisim project p01-3.circ as structural Verilog: 3 circuits, main circuit main
module main (
);

  work work_1 ();  // open: A, B, C, CK1, CK2, A2, B2, C2, f, g
endmodule

module work (
  input  A,
  input  B,
  input  C,
  input  CK1,
  input  CK2,
  output A2,
  output B2,
  output C2,
  output f,
  output g
);

  wire and_1_out, and_2_out, and_3_out, and_4_out, and_5_out, and_6_out, and_7_out, and_8_out, and_9_out,
       and_10_out, and_11_out, and_12_out, and_13_out, and_14_out, and_15_out, and_16_out, and_17_out,
       and_18_out, not_1_out, not_2_out, not_3_out, not_4_out, not_5_out, not_6_out, not_7_out, not_8_out,
       not_9_out, not_10_out, not_11_out, not_12_out, not_13_out, not_14_out, not_15_out, not_16_out,
       not_17_out, not_18_out, not_19_out, not_20_out, not_21_out, not_22_out, not_23_out, not_24_out,
       not_25_out, not_26_out, not_27_out, not_28_out, not_29_out, not_30_out, not_31_out, not_32_out;

  not not_1 (not_1_out, C);
  not not_2 (not_2_out, CK1);
  not not_3 (not_3_out, CK2);
  not not_4 (not_4_out, CK1);
  not not_5 (not_5_out, B);
  not not_6 (not_6_out, CK1);
  not not_7 (not_7_out, CK1);
  not not_8 (not_8_out, CK2);
  not not_9 (not_9_out, C);
  not not_10 (not_10_out, CK1);
  not not_11 (not_11_out, C);
  not not_12 (not_12_out, CK2);
  not not_13 (not_13_out, A);
  not not_14 (not_14_out, B);
  not not_15 (not_15_out, CK1);
  not not_16 (not_16_out, CK2);
  not not_17 (not_17_out, CK2);
  not not_18 (not_18_out, A);
  not not_19 (not_19_out, C);
  not not_20 (not_20_out, CK1);
  not not_21 (not_21_out, A);
  not not_22 (not_22_out, B);
  not not_23 (not_23_out, C);
  not not_24 (not_24_out, A);
  not not_25 (not_25_out, C);
  not not_26 (not_26_out, CK2);
  not not_27 (not_27_out, CK1);
  not not_28 (not_28_out, CK2);
  not not_29 (not_29_out, C);
  not not_30 (not_30_out, CK1);
  not not_31 (not_31_out, CK2);
  not not_32 (not_32_out, CK1);
  and and_1 (and_1_out, B, not_1_out, not_2_out, not_3_out);
  and and_2 (and_2_out, B, C, not_4_out, CK2);
  and and_3 (and_3_out, not_5_out, C, not_6_out);
  and and_4 (and_4_out, C, not_7_out, not_8_out);
  and and_5 (and_5_out, B, not_9_out, not_10_out, CK2);
  and and_6 (and_6_out, B, not_11_out, CK1, not_12_out);
  and and_7 (and_7_out, B, C, CK1, CK2);
  and and_8 (and_8_out, not_13_out, not_14_out, not_15_out, not_16_out);
  and and_9 (and_9_out, C, CK1, CK2);
  and and_10 (and_10_out, B, CK1, CK2);
  and and_11 (and_11_out, B, C, not_17_out);
  and and_12 (and_12_out, not_18_out, not_19_out, not_20_out, CK2);
  and and_13 (and_13_out, not_21_out, not_22_out, not_23_out, CK1);
  and and_14 (and_14_out, not_24_out, not_25_out, CK1, not_26_out);
  and and_15 (and_15_out, C, CK1, CK2);
  and and_16 (and_16_out, B, C, not_27_out, not_28_out);
  and and_17 (and_17_out, B, not_29_out, not_30_out, not_31_out);
  and and_18 (and_18_out, B, C, not_32_out, CK2);
  or or_1 (A2, and_1_out, and_2_out);
  or or_2 (B2, and_3_out, and_4_out, and_5_out, and_6_out, and_7_out);
  or or_3 (C2, and_8_out, and_9_out, and_10_out, and_11_out);
  or or_4 (f, and_12_out, and_13_out, and_14_out, and_15_out, and_16_out);
  or or_5 (g, and_17_out, and_18_out);
endmodule

module navigation (
  input  in_1,
  input  [1:0] in_2,
  input  in_3,
  output out_4,
  output out_5
);

  wire [2:0] register_1_q;
  wire [4:0] work_1_a2;

  work work_1 (
    .A(register_1_q[0]), .B(register_1_q[1]), .C(register_1_q[2]), .CK1(in_2[1]), .CK2(in_2[0]),
    .A2(work_1_a2[0]), .B2(work_1_a2[1]), .C2(work_1_a2[2]), .f(work_1_a2[3]), .g(work_1_a2[4]));
  Register #(.width(5)) register_1 (
    .D(work_1_a2), .Q({out_5, out_4, register_1_q}), .clk(in_1), .clr(in_3));  // open: en
endmodule
