// Logisim project p01-4.circ as structural Verilog: 3 circuits, main circuit main
module main (
  input  [1:0] in_1,
  output out_2
);

  wire _1, _2, _3;
  wire [2:0] register_1_q;

  trans trans_1 (
    .A(register_1_q[2]), .B(register_1_q[1]), .C(register_1_q[0]), .CK1(in_1[1]), .CK2(in_1[0]), .A1(_1),
    .B1(_2), .C1(_3), .PJ(out_2));
  Register #(.width(3)) register_1 (.D({_1, _2, _3}), .Q(register_1_q));  // open: en, clk, clr
endmodule

module trans (
  input  A,
  input  B,
  input  C,
  input  CK1,
  input  CK2,
  output A1,
  output B1,
  output C1,
  output PJ
);

  wire and_3_out, and_4_out, not_1_out, not_2_out, not_3_out, not_4_out, not_5_out, not_6_out, not_7_out;

  not not_1 (not_1_out, CK2);
  not not_2 (not_2_out, B);
  not not_3 (not_3_out, CK2);
  not not_4 (not_4_out, CK1);
  not not_5 (not_5_out, B);
  not not_6 (not_6_out, CK2);
  not not_7 (not_7_out, CK2);
  and and_1 (A1, B, not_1_out);
  and and_2 (B1, not_2_out, C, not_3_out);
  and and_3 (and_3_out, not_4_out, CK2);
  and and_4 (and_4_out, not_5_out, C, CK1, not_6_out);
  and and_5 (PJ, B, not_7_out);
  or or_1 (C1, and_3_out, and_4_out);
endmodule

module fsm (
  input  [1:0] in_1,
  input  in_2,
  output out_3
);

  wire _1, _2, _3, clock_1_out, not_1_out;
  wire [2:0] multiplexer_1_out, register_1_q;

  trans trans_1 (
    .A(register_1_q[2]), .B(register_1_q[1]), .C(register_1_q[0]), .CK1(in_1[1]), .CK2(in_1[0]), .A1(_1),
    .B1(_2), .C1(_3), .PJ(out_3));
  not not_1 (not_1_out, in_2);
  Multiplexer #(.width(3)) multiplexer_1 (
    .in0(3'b000), .in1({_1, _2, _3}), .out(multiplexer_1_out), .sel(not_1_out));  // open: en
  Clock clock_1 (.out(clock_1_out));
  Register #(.width(3)) register_1 (.D(multiplexer_1_out), .Q(register_1_q), .clk(clock_1_out));  // open: en, clr
endmodule
