// Logisim project p0附加题.circ as structural Verilog: 2 circuits, main circuit main
module main (
  input  [15:0] in_1,
  output [31:0] out_2
);

  wire de, \end , neg, not_1_out, or_1_out, \为0 ;
  wire [4:0] right, subtractor_2_out, true;
  wire [31:0] adder_2_out, multiplexer_2_out, negator_1_out, nom, out, part1, shifter_1_out;

  Comparator #(.width(5)) comparator_1 (.a(in_1[14:10]), .b({5{1'b1}}), .eq(\end ));  // open: gt, lt
  Comparator #(.width(5)) comparator_2 (.a(in_1[14:10]), .b({5{1'b0}}), .eq(de));  // open: gt, lt
  Shifter #(.width(32)) shifter_1 (.in(32'h1), .\dist (true), .out(shifter_1_out));
  Subtractor #(.width(5)) subtractor_1 (.a(in_1[14:10]), .b(5'b01111), .out(true));  // open: bin, bout
  Subtractor #(.width(5)) subtractor_2 (.a({5{1'b1}}), .b(true), .out(subtractor_2_out));  // open: bin, bout
  Shifter #(.width(32), .shift("lr")) shifter_2 (.in({in_1[9:0], {22{1'b0}}}), .\dist (right), .out(part1));
  Adder #(.width(5)) adder_1 (.a(subtractor_2_out), .b(5'b00001), .out(right));  // open: cin, cout
  Adder #(.width(32)) adder_2 (.a(shifter_1_out), .b(part1), .out(adder_2_out));  // open: cin, cout
  or or_1 (or_1_out, de, neg);
  Comparator #(.width(5)) comparator_3 (.a(true), .b({5{1'b0}}), .eq(\为0 ), .lt(neg));  // open: gt
  Multiplexer #(.width(32)) multiplexer_1 (.in0(out), .in1({32{1'b0}}), .out(out_2), .sel(\end ));  // open: en
  Multiplexer #(.width(32)) multiplexer_2 (
    .in0(adder_2_out), .in1(32'h1), .out(multiplexer_2_out), .sel(\为0 ));  // open: en
  Multiplexer #(.width(32)) multiplexer_3 (.in0(nom), .in1({32{1'b0}}), .out(out), .sel(or_1_out));  // open: en
  Negator #(.width(32)) negator_1 (.in(multiplexer_2_out), .out(negator_1_out));
  Multiplexer #(.width(32)) multiplexer_4 (
    .in0(negator_1_out), .in1(multiplexer_2_out), .out(nom), .sel(not_1_out));  // open: en
  not not_1 (not_1_out, in_1[15]);

  // Other names for the same wires on the sheet: check[4:0] = in_1[14:10]; fuhao = in_1[15]; frac[9:0] = in_1[9:0];
  //   now[31:22] = in_1[9:0]
endmodule

module ftoi (
  input  [15:0] in_1,
  output [31:0] out_2
);

  wire de, \end , neg, not_1_out, or_1_out, \为0 ;
  wire [4:0] right, subtractor_2_out, true;
  wire [31:0] adder_2_out, multiplexer_2_out, negator_1_out, nom, out, part1, shifter_1_out;

  Comparator #(.width(5)) comparator_1 (.a(in_1[14:10]), .b({5{1'b1}}), .eq(\end ));  // open: gt, lt
  Comparator #(.width(5)) comparator_2 (.a(in_1[14:10]), .b({5{1'b0}}), .eq(de));  // open: gt, lt
  Shifter #(.width(32)) shifter_1 (.in(32'h1), .\dist (true), .out(shifter_1_out));
  Subtractor #(.width(5)) subtractor_1 (.a(in_1[14:10]), .b(5'b01111), .out(true));  // open: bin, bout
  Subtractor #(.width(5)) subtractor_2 (.a({5{1'b1}}), .b(true), .out(subtractor_2_out));  // open: bin, bout
  Shifter #(.width(32), .shift("lr")) shifter_2 (.in({in_1[9:0], {22{1'b0}}}), .\dist (right), .out(part1));
  Adder #(.width(5)) adder_1 (.a(subtractor_2_out), .b(5'b00001), .out(right));  // open: cin, cout
  Adder #(.width(32)) adder_2 (.a(shifter_1_out), .b(part1), .out(adder_2_out));  // open: cin, cout
  or or_1 (or_1_out, de, neg);
  Comparator #(.width(5)) comparator_3 (.a(true), .b({5{1'b0}}), .eq(\为0 ), .lt(neg));  // open: gt
  Multiplexer #(.width(32)) multiplexer_1 (.in0(out), .in1({32{1'b0}}), .out(out_2), .sel(\end ));  // open: en
  Multiplexer #(.width(32)) multiplexer_2 (
    .in0(adder_2_out), .in1(32'h1), .out(multiplexer_2_out), .sel(\为0 ));  // open: en
  Multiplexer #(.width(32)) multiplexer_3 (.in0(nom), .in1({32{1'b0}}), .out(out), .sel(or_1_out));  // open: en
  Negator #(.width(32)) negator_1 (.in(multiplexer_2_out), .out(negator_1_out));
  Multiplexer #(.width(32)) multiplexer_4 (
    .in0(negator_1_out), .in1(multiplexer_2_out), .out(nom), .sel(not_1_out));  // open: en
  not not_1 (not_1_out, in_1[15]);

  // Other names for the same wires on the sheet: check[4:0] = in_1[14:10]; fuhao = in_1[15]; frac[9:0] = in_1[9:0];
  //   now[31:22] = in_1[9:0]
endmodule
