// Logisim project mips单周期cpu1.0.circ as structural Verilog: 6 circuits, main circuit main
module main (
  input  in_1,
  output [31:0] out_2,
  output out_3,
  output [4:0] out_4,
  output [31:0] out_5,
  output out_6,
  output [4:0] out_7,
  output [31:0] out_8
);

  wire ALUSrc, and_1_out, beq, clk, iszero, lui, MemRead, MemtoReg, ori, RegDst;
  wire [1:0] ALUop;
  wire [2:0] ALUCtrl;
  wire [4:0] rd, rs, rt;
  wire [5:0] \function , op;
  wire [15:0] imm;
  wire [31:0] adder_1_out, adder_2_out, ALUout, bigimm, DRAMout, grf_1_out_9, multiplexer_2_out,
       multiplexer_5_out, multiplexer_6_out, nextPC, PC_q, shifter_1_out, signimm, unsign;

  Register #(.width(32)) PC (.D(nextPC), .Q(PC_q), .clk(clk), .clr(in_1));  // open: en
  Clock clock_1 (.out(clk));
  Multiplexer #(.width(5)) multiplexer_1 (.in0(rt), .in1(rd), .out(out_4), .sel(RegDst));  // open: en
  Multiplexer #(.width(32)) multiplexer_2 (
    .in0({ALUout[31:7], out_7, ALUout[1:0]}), .in1(DRAMout), .out(multiplexer_2_out), .sel(MemtoReg));  // open: en
  Adder #(.width(32)) adder_1 (.a(PC_q), .b(32'h4), .out(adder_1_out));  // open: cin, cout
  Shifter #(.width(32)) shifter_1 (.in(signimm), .\dist (5'b00010), .out(shifter_1_out));
  Multiplexer #(.width(32)) multiplexer_3 (.in0(multiplexer_2_out), .in1(bigimm), .out(out_5), .sel(lui));  // open: en
  ROM #(.addrWidth(5), .dataWidth(32)) rom_1 (.addr(PC_q[6:2]), .data(out_2));  // open: sel
  Adder #(.width(32)) adder_2 (.a(adder_1_out), .b(shifter_1_out), .out(adder_2_out));  // open: cin, cout
  grf grf_1 (
    .clk(clk), .reset(in_1), .in_4(out_3), .in_7(rs), .in_6(rt), .in_5(out_4), .in_3(out_5),
    .out_9(grf_1_out_9), .out_8(out_8));
  spliter spliter_1 (.in_1(out_2), .out_2(imm), .out_3(\function ), .rd(rd), .rt(rt), .rs(rs), .out_7(op));
  Multiplexer #(.width(32)) multiplexer_4 (
    .in0(adder_1_out), .in1(adder_2_out), .out(nextPC), .sel(and_1_out));  // open: en
  and and_1 (and_1_out, beq, iszero);
  Multiplexer #(.width(32)) multiplexer_5 (
    .in0(out_8), .in1(signimm), .out(multiplexer_5_out), .sel(ALUSrc));  // open: en
  Multiplexer #(.width(32)) multiplexer_6 (
    .in0(multiplexer_5_out), .in1(unsign), .out(multiplexer_6_out), .sel(ori));  // open: en
  assign signimm = {{16{imm[15]}}, imm};  // Bit_Extender bit_extender_1
  assign unsign = {{16{1'b0}}, imm};  // Bit_Extender bit_extender_2
  ALUcontrl alucontrl_1 (.fuc(\function ), .in_2(ALUop), .out_3(ALUCtrl));
  ALU alu_1 (
    .in_1(grf_1_out_9), .in_2(ALUCtrl), .in_3(multiplexer_6_out), .out_5(iszero),
    .out_4({ALUout[31:7], out_7, ALUout[1:0]}));
  Shifter #(.width(32)) shifter_2 (.in(unsign), .\dist (5'b10000), .out(bigimm));
  control control_1 (
    .op(op), .beq(beq), .out_3(MemtoReg), .MeMwrite(out_6), .MeMread(MemRead), .regwrite(out_3),
    .regdist(RegDst), .ALUSrc(ALUSrc), .ALUctrl1(ALUop[1]), .ALUctrl2(ALUop[0]), .lui(lui), .ori(ori));
  RAM #(.addrWidth(5), .dataWidth(32), .bus("separate")) ram_1 (
    .addr(out_7), .din(out_8), .data(DRAMout), .str(out_6), .clk(clk), .ld(MemRead), .clr(in_1));  // open: sel

  // Other names for the same wires on the sheet: ALUout[6:2] = out_7; DMaddr[4:0] = out_7; intr[31:0] = out_2;
  //   MemWrite = out_6; regaddr[4:0] = out_4; regdata[31:0] = out_5; RegWrite = out_3; reset = in_1;
  //   Rrt[31:0] = out_8

  // Notes on the sheet:
  //   IM
  //   clk
  //   RA1
  //   RA2
  //   WA
  //   WD
  //   contents of rom_1 (hex, n*v repeats v):
  //   3c0b012c 35080004 1084821 ad280008 8d2a0008 1148fffa
  //   WE
  //   reset
  //   RD1
  //   RD2
  //   ALU contrl
  //   DM
  //   main contrl
endmodule

module grf (
  input  clk,
  input  reset,
  input  [31:0] in_3,
  input  in_4,
  input  [4:0] in_5,
  input  [4:0] in_6,
  input  [4:0] in_7,
  output [31:0] out_8,
  output [31:0] out_9
);

  wire [31:0] in2, in3, in4, in5, in6, in7, in8, in9, in10, in11, in12, in13, in14, in15, in16, in17, in18,
       in19, in20, in21, in22, in23, in24, in25, in26, in27, in28, in29, in30, in31, in32, out2, out3, out4,
       out5, out6, out7, out8, out9, out10, out11, out12, out13, out14, out15, out16, out17, out18, out19,
       out20, out21, out22, out23, out24, out25, out26, out27, out28, out29, out30, out31, out32;

  Register #(.width(32)) register_1 (.clk(clk), .clr(reset));  // open: D, en, Q
  Register #(.width(32)) register_2 (.D(in11), .Q(out11), .clk(clk), .clr(reset));  // open: en
  Register #(.width(32)) register_3 (.D(in21), .Q(out21), .clk(clk), .clr(reset));  // open: en
  Register #(.width(32)) register_4 (.D(in31), .Q(out31), .clk(clk), .clr(reset));  // open: en
  Register #(.width(32)) register_5 (.D(in2), .Q(out2), .clk(clk), .clr(reset));  // open: en
  Register #(.width(32)) register_6 (.D(in12), .Q(out12), .clk(clk), .clr(reset));  // open: en
  Register #(.width(32)) register_7 (.D(in22), .Q(out22), .clk(clk), .clr(reset));  // open: en
  Register #(.width(32)) register_8 (.D(in32), .Q(out32), .clk(clk), .clr(reset));  // open: en
  Register #(.width(32)) register_9 (.D(in3), .Q(out3), .clk(clk), .clr(reset));  // open: en
  Register #(.width(32)) register_10 (.D(in13), .Q(out13), .clk(clk), .clr(reset));  // open: en
  Register #(.width(32)) register_11 (.D(in23), .Q(out23), .clk(clk), .clr(reset));  // open: en
  Multiplexer #(.select(5), .width(32), .enable("false")) multiplexer_1 (
    .in0({32{1'b0}}), .in1(out2), .in2(out3), .in3(out4), .in4(out5), .in5(out6), .in6(out7), .in7(out8),
    .in8(out9), .in9(out10), .in10(out11), .in11(out12), .in12(out13), .in13(out14), .in14(out15),
    .in15(out16), .in16(out17), .in17(out18), .in18(out19), .in19(out20), .in20(out21), .in21(out22),
    .in22(out23), .in23(out24), .in24(out25), .in25(out26), .in26(out27), .in27(out28), .in28(out29),
    .in29(out30), .in30(out31), .in31(out32), .out(out_9), .sel(in_7));
  Register #(.width(32)) register_12 (.D(in4), .Q(out4), .clk(clk), .clr(reset));  // open: en
  Register #(.width(32)) register_13 (.D(in14), .Q(out14), .clk(clk), .clr(reset));  // open: en
  Register #(.width(32)) register_14 (.D(in24), .Q(out24), .clk(clk), .clr(reset));  // open: en
  Register #(.width(32)) register_15 (.D(in5), .Q(out5), .clk(clk), .clr(reset));  // open: en
  Register #(.width(32)) register_16 (.D(in15), .Q(out15), .clk(clk), .clr(reset));  // open: en
  Register #(.width(32)) register_17 (.D(in25), .Q(out25), .clk(clk), .clr(reset));  // open: en
  Register #(.width(32)) register_18 (.D(in6), .Q(out6), .clk(clk), .clr(reset));  // open: en
  Register #(.width(32)) register_19 (.D(in16), .Q(out16), .clk(clk), .clr(reset));  // open: en
  Register #(.width(32)) register_20 (.D(in26), .Q(out26), .clk(clk), .clr(reset));  // open: en
  Multiplexer #(.select(5), .width(32), .enable("false")) multiplexer_2 (
    .in0({32{1'b0}}), .in1(out2), .in2(out3), .in3(out4), .in4(out5), .in5(out6), .in6(out7), .in7(out8),
    .in8(out9), .in9(out10), .in10(out11), .in11(out12), .in12(out13), .in13(out14), .in14(out15),
    .in15(out16), .in16(out17), .in17(out18), .in18(out19), .in19(out20), .in20(out21), .in21(out22),
    .in22(out23), .in23(out24), .in24(out25), .in25(out26), .in26(out27), .in27(out28), .in28(out29),
    .in29(out30), .in30(out31), .in31(out32), .out(out_8), .sel(in_6));
  Register #(.width(32)) register_21 (.D(in7), .Q(out7), .clk(clk), .clr(reset));  // open: en
  Register #(.width(32)) register_22 (.D(in17), .Q(out17), .clk(clk), .clr(reset));  // open: en
  Register #(.width(32)) register_23 (.D(in27), .Q(out27), .clk(clk), .clr(reset));  // open: en
  Register #(.width(32)) register_24 (.D(in8), .Q(out8), .clk(clk), .clr(reset));  // open: en
  Register #(.width(32)) register_25 (.D(in18), .Q(out18), .clk(clk), .clr(reset));  // open: en
  Register #(.width(32)) register_26 (.D(in28), .Q(out28), .clk(clk), .clr(reset));  // open: en
  Demultiplexer #(.select(5), .width(32), .tristate("true")) demultiplexer_1 (
    .out1(in2), .out2(in3), .out3(in4), .out4(in5), .out5(in6), .out6(in7), .out7(in8), .out8(in9),
    .out9(in10), .out10(in11), .out11(in12), .out12(in13), .out13(in14), .out14(in15), .out15(in16),
    .out16(in17), .out17(in18), .out18(in19), .out19(in20), .out20(in21), .out21(in22), .out22(in23),
    .out23(in24), .out24(in25), .out25(in26), .out26(in27), .out27(in28), .out28(in29), .out29(in30),
    .out30(in31), .out31(in32), .in(in_3), .sel(in_5), .en(in_4));  // open: out0
  Register #(.width(32)) register_27 (.D(in9), .Q(out9), .clk(clk), .clr(reset));  // open: en
  Register #(.width(32)) register_28 (.D(in19), .Q(out19), .clk(clk), .clr(reset));  // open: en
  Register #(.width(32)) register_29 (.D(in29), .Q(out29), .clk(clk), .clr(reset));  // open: en
  Register #(.width(32)) register_30 (.D(in10), .Q(out10), .clk(clk), .clr(reset));  // open: en
  Register #(.width(32)) register_31 (.D(in20), .Q(out20), .clk(clk), .clr(reset));  // open: en
  Register #(.width(32)) register_32 (.D(in30), .Q(out30), .clk(clk), .clr(reset));  // open: en

  // Other names for the same wires on the sheet: clear = reset
endmodule

module ALU (
  input  [31:0] in_1,
  input  [2:0] in_2,
  input  [31:0] in_3,
  output [31:0] out_4,
  output out_5
);

  wire [31:0] add, minus, \or ;

  Adder #(.width(32)) adder_1 (.a(in_1), .b(in_3), .out(add));  // open: cin, cout
  Subtractor #(.width(32)) subtractor_1 (.a(in_1), .b(in_3), .out(minus));  // open: bin, bout
  assign \or  = in_1 | in_3;  // OR_Gate or_1, 32 bits wide
  Multiplexer #(.select(3), .width(32), .disabled(0), .enable("false")) multiplexer_1 (
    .in0(add), .in1(add), .in2(minus), .in4(\or ), .out(out_4), .sel(in_2));  // open: in3, in5, in6, in7
  Comparator #(.width(32)) comparator_1 (.a(out_4), .b({32{1'b0}}), .eq(out_5));  // open: gt, lt

  // Other names for the same wires on the sheet: A[31:0] = in_1; B[31:0] = in_3; check[31:0] = out_4
endmodule

module control (
  input  [5:0] op,
  output beq,
  output out_3,
  output MeMwrite,
  output MeMread,
  output regwrite,
  output regdist,
  output ALUSrc,
  output ALUctrl1,
  output ALUctrl2,
  output lui,
  output ori
);

  wire not_1_out, not_2_out, not_3_out, not_4_out, not_5_out, not_6_out;

  not not_1 (not_1_out, op[5]);
  not not_2 (not_2_out, op[4]);
  not not_3 (not_3_out, op[3]);
  not not_4 (not_4_out, op[1]);
  not not_5 (not_5_out, op[2]);
  not not_6 (not_6_out, op[0]);
  and and_1 (regdist, not_1_out, not_2_out, not_3_out, not_5_out, not_4_out, not_6_out);
  and and_2 (MeMread, op[5], not_2_out, not_3_out, not_5_out, op[1], op[0]);
  and and_3 (ori, not_1_out, not_2_out, op[3], op[2], not_4_out, op[0]);
  and and_4 (MeMwrite, op[5], not_2_out, op[3], not_5_out, op[1], op[0]);
  and and_5 (beq, not_1_out, not_2_out, not_3_out, op[2], not_4_out, not_6_out);
  and and_6 (lui, not_1_out, not_2_out, op[3], op[2], op[1], op[0]);
  or or_1 (regwrite, regdist, MeMread, ori, lui);
  or or_2 (ALUSrc, MeMread, MeMwrite);
  or or_3 (ALUctrl1, regdist, beq);
  or or_4 (ALUctrl2, ori, beq);

  assign out_3 = MeMread;

  // Notes on the sheet:
  //   R
  //   lw
  //   ori
  //   sw
  //   beq
  //   lui
  //   memtoreg
endmodule

module spliter (
  input  [31:0] in_1,
  output [15:0] out_2,
  output [5:0] out_3,
  output [4:0] rd,
  output [4:0] rt,
  output [4:0] rs,
  output [5:0] out_7
);


  assign out_2 = in_1[15:0];
  assign out_3 = in_1[5:0];
  assign out_7 = in_1[31:26];
  assign rd = in_1[15:11];
  assign rs = in_1[25:21];
  assign rt = in_1[20:16];

  // Other names for the same wires on the sheet: _6 = in_1[0]; _7 = in_1[1]; _8 = in_1[2]; _9 = in_1[3];
  //   _10 = in_1[4]; _11 = in_1[5]; _1 = in_1[11]; _2 = in_1[12]; _3 = in_1[13]; _4 = in_1[14]; _5 = in_1[15];
  //   in = in_1[20]

  // Notes on the sheet:
  //   imm
  //   op
  //   fuction
endmodule

module ALUcontrl (
  input  [5:0] fuc,
  input  [1:0] in_2,
  output [2:0] out_3
);

  wire and_1_out, and_2_out, and_4_out, and_5_out, and_6_out, and_7_out, not_1_out, not_2_out, not_3_out,
       not_4_out, not_5_out, not_6_out, not_7_out, not_8_out;

  not not_1 (not_1_out, fuc[4]);
  not not_2 (not_2_out, fuc[5]);
  not not_3 (not_3_out, fuc[3]);
  not not_4 (not_4_out, fuc[1]);
  not not_5 (not_5_out, fuc[2]);
  not not_6 (not_6_out, fuc[0]);
  and and_1 (and_1_out, fuc[5], not_1_out, not_3_out, not_5_out, not_4_out, fuc[0]);
  and and_2 (and_2_out, fuc[5], not_1_out, not_3_out, not_5_out, fuc[1], fuc[0]);
  not not_7 (not_7_out, in_2[1]);
  not not_8 (not_8_out, in_2[0]);
  and and_3 (out_3[2], not_7_out, in_2[0]);
  and and_4 (and_4_out, in_2[1], not_8_out, and_1_out);
  and and_5 (and_5_out, not_8_out, not_7_out);
  and and_6 (and_6_out, in_2[1], in_2[0]);
  and and_7 (and_7_out, in_2[1], not_8_out, and_2_out);
  or or_1 (out_3[1], and_6_out, and_7_out);
  or or_2 (out_3[0], and_4_out, and_5_out);

  // Notes on the sheet:
  //   addu
  //   subu
  //   R-add
  //   lw,sw+
  //   ori-or
  //   beq-minus
  //   R-subu
endmodule
