// Logisim project mips单周期cpu1.2.circ as structural Verilog: 8 circuits, main circuit main
module main (
  input  in_1,
  output [31:0] out_2,
  output out_3,
  output [4:0] out_4,
  output [31:0] out_5,
  output out_6,
  output [4:0] out_7,
  output [31:0] out_8
);

  wire ALUSrc, and_1_out, beq, clk, isj, iszero, jal, jr, lui, MemRead, MemtoReg, or_1_out, ori, RegDst;
  wire [2:0] ALUCtrl;
  wire [4:0] multiplexer_1_out, rd, rs, rt;
  wire [5:0] \function , op;
  wire [15:0] imm;
  wire [25:0] j;
  wire [27:0] PC;
  wire [31:0] adder_2_out, ALUout, bigimm, DRAMout, multiplexer_2_out, multiplexer_4_out, multiplexer_6_out,
       multiplexer_7_out, multiplexer_9_out, multiplexer_10_out, nextPC, PC_4, Rrs, shifter_1_out, signimm,
       unsign;
  wire [31:28] jalPC;

  Clock clock_1 (.out(clk));
  Multiplexer #(.width(5)) multiplexer_1 (.in0(rt), .in1(rd), .out(multiplexer_1_out), .sel(RegDst));  // open: en
  Multiplexer #(.width(32)) multiplexer_2 (
    .in0({ALUout[31:7], out_7, ALUout[1:0]}), .in1(DRAMout), .out(multiplexer_2_out), .sel(MemtoReg));  // open: en
  IFU IFU (.in_1(nextPC), .out_4(out_2), .in_2(clk), .in_3(in_1), .out_5({jalPC, PC}));
  Adder #(.width(32)) adder_1 (.a({jalPC, PC}), .b(32'h4), .out(PC_4));  // open: cin, cout
  Shifter #(.width(32)) shifter_1 (.in(signimm), .\dist (5'b00010), .out(shifter_1_out));
  Multiplexer #(.width(5)) multiplexer_3 (
    .in0(multiplexer_1_out), .in1({5{1'b1}}), .out(out_4), .sel(jal));  // open: en
  Multiplexer #(.width(32)) multiplexer_4 (
    .in0(multiplexer_2_out), .in1(bigimm), .out(multiplexer_4_out), .sel(lui));  // open: en
  Adder #(.width(32)) adder_2 (.a(PC_4), .b(shifter_1_out), .out(adder_2_out));  // open: cin, cout
  Multiplexer #(.width(32)) multiplexer_5 (.in0(multiplexer_4_out), .in1(PC_4), .out(out_5), .sel(jal));  // open: en
  Multiplexer #(.width(32)) multiplexer_6 (
    .in0(PC_4), .in1(adder_2_out), .out(multiplexer_6_out), .sel(and_1_out));  // open: en
  and and_1 (and_1_out, beq, iszero);
  grf grf_1 (
    .clk(clk), .reset(in_1), .in_4(out_3), .in_7(rs), .in_6(rt), .in_5(out_4), .in_3(out_5), .out_9(Rrs),
    .out_8(out_8));
  or or_1 (or_1_out, jal, isj);
  spliter spliter_1 (.in_1(out_2), .out_2(imm), .out_3(\function ), .rd(rd), .rt(rt), .rs(rs), .out_7(op), .out_8(j));
  Multiplexer #(.width(32)) multiplexer_7 (
    .in0(multiplexer_6_out), .in1({jalPC, j, 2'b00}), .out(multiplexer_7_out), .sel(or_1_out));  // open: en
  Multiplexer #(.width(32)) multiplexer_8 (.in0(multiplexer_7_out), .in1(Rrs), .out(nextPC), .sel(jr));  // open: en
  Multiplexer #(.width(32)) multiplexer_9 (
    .in0(out_8), .in1(signimm), .out(multiplexer_9_out), .sel(ALUSrc));  // open: en
  control control_1 (
    .op(op), .beq(beq), .out_5(MemtoReg), .MeMwrite(out_6), .MeMread(MemRead), .regwrite(out_3),
    .regdist(RegDst), .ALUSrc(ALUSrc), .lui(lui), .ori(ori), .in_2(\function ), .ALUctrl0(ALUCtrl),
    .jal(jal), .jr(jr), .out_15(isj));
  Multiplexer #(.width(32)) multiplexer_10 (
    .in0(multiplexer_9_out), .in1(unsign), .out(multiplexer_10_out), .sel(ori));  // open: en
  EXT ext_1 (.in_1(imm), .out_2(signimm), .out_3(unsign), .out_4(bigimm));
  ALU alu_1 (
    .in_1(Rrs), .in_2(ALUCtrl), .in_3(multiplexer_10_out), .out_5(iszero),
    .out_4({ALUout[31:7], out_7, ALUout[1:0]}));
  RAM #(.addrWidth(5), .dataWidth(32), .bus("separate")) ram_1 (
    .addr(out_7), .din(out_8), .data(DRAMout), .str(out_6), .clk(clk), .ld(MemRead), .clr(in_1));  // open: sel

  // Other names for the same wires on the sheet: ALUout[6:2] = out_7; DMaddr[4:0] = out_7; intr[31:0] = out_2;
  //   jalPC[27:2] = j; MemWrite = out_6; PC[31:28] = jalPC; regaddr[4:0] = out_4; regdata[31:0] = out_5;
  //   RegWrite = out_3; reset = in_1; Rrt[31:0] = out_8

  // Notes on the sheet:
  //   clk
  //   RA1
  //   RA2
  //   WA
  //   WD
  //   WE
  //   reset
  //   RD1
  //   RD2
  //   spliter
  //   main contrl
  //   EXT
  //   DM
endmodule

module grf (
  input  clk,
  input  reset,
  input  [31:0] in_3,
  input  in_4,
  input  [4:0] in_5,
  input  [4:0] in_6,
  input  [4:0] in_7,
  output [31:0] out_8,
  output [31:0] out_9
);

  wire [31:0] in2, in3, in4, in5, in6, in7, in8, in9, in10, in11, in12, in13, in14, in15, in16, in17, in18,
       in19, in20, in21, in22, in23, in24, in25, in26, in27, in28, in29, in30, in31, in32, out2, out3, out4,
       out5, out6, out7, out8, out9, out10, out11, out12, out13, out14, out15, out16, out17, out18, out19,
       out20, out21, out22, out23, out24, out25, out26, out27, out28, out29, out30, out31, out32;

  Register #(.width(32)) register_1 (.clk(clk), .clr(reset));  // open: D, en, Q
  Register #(.width(32)) register_2 (.D(in11), .Q(out11), .clk(clk), .clr(reset));  // open: en
  Register #(.width(32)) register_3 (.D(in21), .Q(out21), .clk(clk), .clr(reset));  // open: en
  Register #(.width(32)) register_4 (.D(in31), .Q(out31), .clk(clk), .clr(reset));  // open: en
  Register #(.width(32)) register_5 (.D(in2), .Q(out2), .clk(clk), .clr(reset));  // open: en
  Register #(.width(32)) register_6 (.D(in12), .Q(out12), .clk(clk), .clr(reset));  // open: en
  Register #(.width(32)) register_7 (.D(in22), .Q(out22), .clk(clk), .clr(reset));  // open: en
  Register #(.width(32)) register_8 (.D(in32), .Q(out32), .clk(clk), .clr(reset));  // open: en
  Register #(.width(32)) register_9 (.D(in3), .Q(out3), .clk(clk), .clr(reset));  // open: en
  Register #(.width(32)) register_10 (.D(in13), .Q(out13), .clk(clk), .clr(reset));  // open: en
  Register #(.width(32)) register_11 (.D(in23), .Q(out23), .clk(clk), .clr(reset));  // open: en
  Multiplexer #(.select(5), .width(32), .enable("false")) multiplexer_1 (
    .in0({32{1'b0}}), .in1(out2), .in2(out3), .in3(out4), .in4(out5), .in5(out6), .in6(out7), .in7(out8),
    .in8(out9), .in9(out10), .in10(out11), .in11(out12), .in12(out13), .in13(out14), .in14(out15),
    .in15(out16), .in16(out17), .in17(out18), .in18(out19), .in19(out20), .in20(out21), .in21(out22),
    .in22(out23), .in23(out24), .in24(out25), .in25(out26), .in26(out27), .in27(out28), .in28(out29),
    .in29(out30), .in30(out31), .in31(out32), .out(out_9), .sel(in_7));
  Register #(.width(32)) register_12 (.D(in4), .Q(out4), .clk(clk), .clr(reset));  // open: en
  Register #(.width(32)) register_13 (.D(in14), .Q(out14), .clk(clk), .clr(reset));  // open: en
  Register #(.width(32)) register_14 (.D(in24), .Q(out24), .clk(clk), .clr(reset));  // open: en
  Register #(.width(32)) register_15 (.D(in5), .Q(out5), .clk(clk), .clr(reset));  // open: en
  Register #(.width(32)) register_16 (.D(in15), .Q(out15), .clk(clk), .clr(reset));  // open: en
  Register #(.width(32)) register_17 (.D(in25), .Q(out25), .clk(clk), .clr(reset));  // open: en
  Register #(.width(32)) register_18 (.D(in6), .Q(out6), .clk(clk), .clr(reset));  // open: en
  Register #(.width(32)) register_19 (.D(in16), .Q(out16), .clk(clk), .clr(reset));  // open: en
  Register #(.width(32)) register_20 (.D(in26), .Q(out26), .clk(clk), .clr(reset));  // open: en
  Multiplexer #(.select(5), .width(32), .enable("false")) multiplexer_2 (
    .in0({32{1'b0}}), .in1(out2), .in2(out3), .in3(out4), .in4(out5), .in5(out6), .in6(out7), .in7(out8),
    .in8(out9), .in9(out10), .in10(out11), .in11(out12), .in12(out13), .in13(out14), .in14(out15),
    .in15(out16), .in16(out17), .in17(out18), .in18(out19), .in19(out20), .in20(out21), .in21(out22),
    .in22(out23), .in23(out24), .in24(out25), .in25(out26), .in26(out27), .in27(out28), .in28(out29),
    .in29(out30), .in30(out31), .in31(out32), .out(out_8), .sel(in_6));
  Register #(.width(32)) register_21 (.D(in7), .Q(out7), .clk(clk), .clr(reset));  // open: en
  Register #(.width(32)) register_22 (.D(in17), .Q(out17), .clk(clk), .clr(reset));  // open: en
  Register #(.width(32)) register_23 (.D(in27), .Q(out27), .clk(clk), .clr(reset));  // open: en
  Register #(.width(32)) register_24 (.D(in8), .Q(out8), .clk(clk), .clr(reset));  // open: en
  Register #(.width(32)) register_25 (.D(in18), .Q(out18), .clk(clk), .clr(reset));  // open: en
  Register #(.width(32)) register_26 (.D(in28), .Q(out28), .clk(clk), .clr(reset));  // open: en
  Demultiplexer #(.select(5), .width(32), .tristate("true")) demultiplexer_1 (
    .out1(in2), .out2(in3), .out3(in4), .out4(in5), .out5(in6), .out6(in7), .out7(in8), .out8(in9),
    .out9(in10), .out10(in11), .out11(in12), .out12(in13), .out13(in14), .out14(in15), .out15(in16),
    .out16(in17), .out17(in18), .out18(in19), .out19(in20), .out20(in21), .out21(in22), .out22(in23),
    .out23(in24), .out24(in25), .out25(in26), .out26(in27), .out27(in28), .out28(in29), .out29(in30),
    .out30(in31), .out31(in32), .in(in_3), .sel(in_5), .en(in_4));  // open: out0
  Register #(.width(32)) register_27 (.D(in9), .Q(out9), .clk(clk), .clr(reset));  // open: en
  Register #(.width(32)) register_28 (.D(in19), .Q(out19), .clk(clk), .clr(reset));  // open: en
  Register #(.width(32)) register_29 (.D(in29), .Q(out29), .clk(clk), .clr(reset));  // open: en
  Register #(.width(32)) register_30 (.D(in10), .Q(out10), .clk(clk), .clr(reset));  // open: en
  Register #(.width(32)) register_31 (.D(in20), .Q(out20), .clk(clk), .clr(reset));  // open: en
  Register #(.width(32)) register_32 (.D(in30), .Q(out30), .clk(clk), .clr(reset));  // open: en

  // Other names for the same wires on the sheet: clear = reset
endmodule

module ALU (
  input  [31:0] in_1,
  input  [2:0] in_2,
  input  [31:0] in_3,
  output [31:0] out_4,
  output out_5
);

  wire [31:0] add, minus, \or ;

  Adder #(.width(32)) adder_1 (.a(in_1), .b(in_3), .out(add));  // open: cin, cout
  Subtractor #(.width(32)) subtractor_1 (.a(in_1), .b(in_3), .out(minus));  // open: bin, bout
  assign \or  = in_1 | in_3;  // OR_Gate or_1, 32 bits wide
  Multiplexer #(.select(3), .width(32), .disabled(0), .enable("false")) multiplexer_1 (
    .in0(add), .in1(minus), .in2(\or ), .out(out_4), .sel(in_2));  // open: in3, in4, in5, in6, in7
  Comparator #(.width(32)) comparator_1 (.a(out_4), .b({32{1'b0}}), .eq(out_5));  // open: gt, lt

  // Other names for the same wires on the sheet: A[31:0] = in_1; B[31:0] = in_3; check[31:0] = out_4
endmodule

module control (
  input  [5:0] op,
  input  [5:0] in_2,
  output [2:0] ALUctrl0,
  output beq,
  output out_5,
  output MeMwrite,
  output MeMread,
  output regwrite,
  output regdist,
  output ALUSrc,
  output lui,
  output ori,
  output jal,
  output jr,
  output out_15
);

  wire addu, and_7_out, and_8_out, jr_t, not_1_out, not_2_out, not_3_out, not_4_out, not_5_out, not_6_out,
       subu;

  ALUcontrl alucontrl_1 (.fuc(in_2), .out_2(addu), .out_3(subu), .out_4(jr_t));
  not not_1 (not_1_out, op[5]);
  not not_2 (not_2_out, op[4]);
  not not_3 (not_3_out, op[3]);
  not not_4 (not_4_out, op[1]);
  not not_5 (not_5_out, op[2]);
  not not_6 (not_6_out, op[0]);
  and and_1 (regdist, not_1_out, not_2_out, not_3_out, not_5_out, not_4_out, not_6_out);
  and and_2 (MeMread, op[5], not_2_out, not_3_out, not_5_out, op[1], op[0]);
  and and_3 (ori, not_1_out, not_2_out, op[3], op[2], not_4_out, op[0]);
  and and_4 (MeMwrite, op[5], not_2_out, op[3], not_5_out, op[1], op[0]);
  and and_5 (beq, not_1_out, not_2_out, not_3_out, op[2], not_4_out, not_6_out);
  and and_6 (lui, not_1_out, not_2_out, op[3], op[2], op[1], op[0]);
  and u_jal (jal, not_1_out, not_2_out, not_3_out, not_5_out, op[1], op[0]);
  and j (out_15, not_1_out, not_2_out, not_3_out, not_5_out, op[1], not_6_out);
  and and_7 (and_7_out, addu, regdist);
  and and_8 (and_8_out, subu, regdist);
  and and_9 (jr, jr_t, regdist);
  or or_1 (regwrite, regdist, MeMread, jal, ori, lui);
  or or_2 (ALUSrc, MeMread, MeMwrite);
  buf or_3 (ALUctrl0[2], 1'b0);  // OR_Gate
  or or_4 (ALUctrl0[0], beq, and_8_out);
  buf or_5 (ALUctrl0[1], ori);  // OR_Gate

  assign out_5 = MeMread;

  // Other names for the same wires on the sheet: R = regdist

  // Notes on the sheet:
  //   R
  //   lw
  //   ori
  //   sw
  //   beq
  //   lui
  //   memtoreg
endmodule

module spliter (
  input  [31:0] in_1,
  output [15:0] out_2,
  output [5:0] out_3,
  output [4:0] rd,
  output [4:0] rt,
  output [4:0] rs,
  output [5:0] out_7,
  output [25:0] out_8
);


  assign out_2 = in_1[15:0];
  assign out_3 = in_1[5:0];
  assign out_7 = in_1[31:26];
  assign out_8 = in_1[25:0];
  assign rd = in_1[15:11];
  assign rs = in_1[25:21];
  assign rt = in_1[20:16];

  // Other names for the same wires on the sheet: _6 = in_1[0]; _7 = in_1[1]; _8 = in_1[2]; _9 = in_1[3];
  //   _10 = in_1[4]; _11 = in_1[5]; _1 = in_1[11]; _2 = in_1[12]; _3 = in_1[13]; _4 = in_1[14]; _5 = in_1[15];
  //   in = in_1[20]

  // Notes on the sheet:
  //   j
  //   imm
  //   op
  //   fuction
endmodule

module ALUcontrl (
  input  [5:0] fuc,
  output out_2,
  output out_3,
  output out_4
);

  wire not_1_out, not_2_out, not_3_out, not_4_out, not_5_out, not_6_out;

  not not_1 (not_1_out, fuc[4]);
  not not_2 (not_2_out, fuc[5]);
  not not_3 (not_3_out, fuc[3]);
  not not_4 (not_4_out, fuc[2]);
  not not_5 (not_5_out, fuc[1]);
  not not_6 (not_6_out, fuc[0]);
  and and_1 (out_2, fuc[5], not_1_out, not_3_out, not_4_out, not_5_out, fuc[0]);
  and and_2 (out_3, fuc[5], not_1_out, not_3_out, not_4_out, fuc[1], fuc[0]);
  and and_3 (out_4, not_2_out, not_1_out, fuc[3], not_4_out, not_5_out, not_6_out);

  // Notes on the sheet:
  //   addu
  //   subu
  //   jr
endmodule

module IFU (
  input  [31:0] in_1,
  input  in_2,
  input  in_3,
  output [31:0] out_4,
  output [31:0] out_5
);

  Register #(.width(32)) PC (.D(in_1), .Q(out_5), .clk(in_2), .clr(in_3));  // open: en
  ROM #(.addrWidth(5), .dataWidth(32)) rom_1 (.addr(out_5[6:2]), .data(out_4));  // open: sel

  // Notes on the sheet:
  //   contents of rom_1 (hex, n*v repeats v):
  //   34010001 34020002 10220001 210821 340c0001 340d0001 118d0001 421021 c000c0c c000c11 c63021 c000c11
  //   1f7821 34050004 3e5f821 1e00008 210821
endmodule

module EXT (
  input  [15:0] in_1,
  output [31:0] out_2,
  output [31:0] out_3,
  output [31:0] out_4
);

  assign out_2 = {{16{in_1[15]}}, in_1};  // Bit_Extender bit_extender_1
  assign out_3 = {{16{1'b0}}, in_1};  // Bit_Extender bit_extender_2
  Shifter #(.width(32)) shifter_1 (.in(out_3), .\dist (5'b10000), .out(out_4));

  // Other names for the same wires on the sheet: imm[15:0] = in_1; unsign[31:0] = out_3
endmodule
