// Logisim project logisimtest3.circ as structural Verilog
module \tran  (
  input  [1:0] in_1,
  input  add,
  output [1:0] out_3
);

  wire and_1_out, and_2_out, and_3_out, and_4_out, and_5_out, and_6_out, not_1_out, not_2_out, not_3_out,
       not_4_out, not_5_out, not_6_out, not_7_out, not_8_out;

  not not_1 (not_1_out, in_1[0]);
  not not_2 (not_2_out, in_1[1]);
  not not_3 (not_3_out, in_1[0]);
  not not_4 (not_4_out, in_1[1]);
  not not_5 (not_5_out, in_1[0]);
  not not_6 (not_6_out, add);
  not not_7 (not_7_out, in_1[1]);
  not not_8 (not_8_out, add);
  and and_1 (and_1_out, not_1_out, in_1[1]);
  and and_2 (and_2_out, in_1[0], not_2_out);
  and and_3 (and_3_out, not_3_out, not_4_out, add);
  and and_4 (and_4_out, not_5_out, in_1[1], not_6_out);
  and and_5 (and_5_out, in_1[0], not_7_out, not_8_out);
  and and_6 (and_6_out, in_1[0], in_1[1], add);
  or or_1 (out_3[0], and_1_out, and_2_out);
  or or_2 (out_3[1], and_3_out, and_4_out, and_5_out, and_6_out);
endmodule

module mod5 (
  input  in_1,
  output out_2,
  output out_3,
  output out_4,
  output out_5,
  output out_6
);

  wire clock_1_out;
  wire [1:0] register_1_q, tran_1_out_3;

  \tran  tran_1 (.in_1(register_1_q), .add(in_1), .out_3(tran_1_out_3));
  Register #(.width(2)) register_1 (.D(tran_1_out_3), .Q(register_1_q), .clk(clock_1_out));  // open: en, clr
  Clock clock_1 (.out(clock_1_out));
  out out_1 (.in_1(tran_1_out_3), .s0(out_2), .s1(out_3), .s2(out_4), .s3(out_5), .s4(out_6));
endmodule

module out (
  input  [1:0] in_1,
  output s0,
  output s1,
  output s2,
  output s3,
  output s4
);

  wire not_1_out, not_2_out, not_3_out, not_4_out;

  not not_1 (not_1_out, in_1[0]);
  not not_2 (not_2_out, in_1[1]);
  not not_3 (not_3_out, in_1[0]);
  not not_4 (not_4_out, in_1[1]);
  and and_1 (s1, not_1_out, not_2_out);
  and and_2 (s2, not_3_out, in_1[1]);
  and and_3 (s3, in_1[0], not_4_out);
  and and_4 (s4, in_1[0], in_1[1]);

  assign s0 = 1'b0;
endmodule
