// Logisim project logisimtest4.circ as structural Verilog: 2 circuits, main circuit main
// power
module main (
  input  [2:0] in_1,
  output [3:0] out_2
);

  wire and_1_out, clock, comparator_1_eq, comparator_1_lt, not_1_out, not_2_out, or_1_out, pose, power, tag;
  wire [2:0] judge;
  wire [3:0] adder_1_out, multiplexer_1_out, register_1_q, register_2_q;

  Counter #(.width(3), .max('h7)) counter_1 (.Q(judge), .carry(pose), .clk(and_1_out));  // open: load, D, count, clr
  not not_1 (not_1_out, pose);
  and and_1 (and_1_out, clock, not_1_out);
  Comparator #(.width(3), .mode("unsigned")) comparator_1 (
    .a(in_1), .b(judge), .eq(comparator_1_eq), .lt(comparator_1_lt));  // open: gt
  Comparator #(.width(3), .mode("unsigned")) comparator_2 (.a(3'b000), .b(judge), .eq(tag));  // open: gt, lt
  Multiplexer #(.width(4)) multiplexer_1 (
    .in0(4'b0001), .in1(adder_1_out), .out(multiplexer_1_out), .sel(not_2_out));  // open: en
  not not_2 (not_2_out, tag);
  or or_1 (or_1_out, comparator_1_eq, comparator_1_lt);
  Register #(.width(4)) register_1 (.D(multiplexer_1_out), .en(power), .Q(register_1_q), .clk(clock));  // open: clr
  Register #(.width(4)) register_2 (.D(register_1_q), .en(power), .Q(register_2_q), .clk(clock));  // open: clr
  Clock clock_1 (.out(clock));
  not not_3 (power, or_1_out);
  Adder #(.width(4)) adder_1 (.a(register_1_q), .b(register_2_q), .out(adder_1_out));  // open: cin, cout
  Multiplexer #(.width(4)) multiplexer_2 (.in0(register_1_q), .in1(4'b0000), .out(out_2), .sel(power));  // open: en
endmodule

module out (
  input  [3:0] in_1,
  input  in_2,
  output [3:0] out_3
);

  and and_1 (out_3[0], in_1[0], in_2);
  and and_2 (out_3[1], in_1[1], in_2);
  and and_3 (out_3[2], in_1[2], in_2);
  and and_4 (out_3[3], in_1[3], in_2);
endmodule
