// Logisim project logisimtest5.circ as structural Verilog: 2 circuits, main circuit main
// power
module main (
  input  [31:0] in_1,
  output [31:0] out_2
);

  wire and_1_out, check, clock, comparator_1_eq, comparator_1_lt, comparator_2_eq, ini, not_1_out, pose, tag;
  wire [31:0] a, aa, aa1, and_2_out, b, bb, bb1, c, cc, cc1, d, dd, dd1, e, ee, f, ff, g, gg, h, hh,
       multiplexer_1_out, multiplexer_2_out, multiplexer_3_out, multiplexer_4_out, multiplexer_5_out,
       multiplexer_6_out, multiplexer_7_out, multiplexer_8_out, multiplexer_9_out, now, register_9_q,
       shifter_1_out;

  not not_1 (not_1_out, pose);
  Clock clock_1 (.out(clock));
  and and_1 (and_1_out, clock, not_1_out);
  Counter #(.width(32), .max('h80)) counter_1 (.Q(now), .carry(pose), .clk(and_1_out));  // open: load, D, count, clr
  Comparator #(.width(32), .mode("unsigned")) comparator_1 (
    .a(32'h21), .b(now), .eq(comparator_1_eq), .lt(comparator_1_lt));  // open: gt
  not not_2 (ini, comparator_2_eq);
  Comparator #(.width(32), .mode("unsigned")) comparator_2 (
    .a({32{1'b0}}), .b(now), .eq(comparator_2_eq));  // open: gt, lt
  or or_1 (tag, comparator_1_eq, comparator_1_lt);
  Multiplexer #(.width(32)) multiplexer_1 (.in0(32'h1), .in1(aa), .out(multiplexer_1_out), .sel(ini));  // open: en
  Multiplexer #(.width(32)) multiplexer_2 (.in0({32{1'b0}}), .in1(bb), .out(multiplexer_2_out), .sel(ini));  // open: en
  Multiplexer #(.width(32)) multiplexer_3 (.in0({32{1'b0}}), .in1(cc), .out(multiplexer_3_out), .sel(ini));  // open: en
  Multiplexer #(.width(32)) multiplexer_4 (.in0(32'h1), .in1(dd), .out(multiplexer_4_out), .sel(ini));  // open: en
  Multiplexer #(.width(32)) multiplexer_5 (.in0({32{1'b0}}), .in1(ee), .out(multiplexer_5_out), .sel(ini));  // open: en
  Multiplexer #(.width(32)) multiplexer_6 (.in0(32'h1), .in1(ff), .out(multiplexer_6_out), .sel(ini));  // open: en
  Multiplexer #(.width(32)) multiplexer_7 (.in0(32'h1), .in1(gg), .out(multiplexer_7_out), .sel(ini));  // open: en
  Multiplexer #(.width(32)) multiplexer_8 (.in0(32'h1), .in1(hh), .out(multiplexer_8_out), .sel(ini));  // open: en
  Register #(.width(32)) register_1 (.D(multiplexer_1_out), .Q(a), .clk(clock));  // open: en, clr
  Register #(.width(32)) register_2 (.D(multiplexer_2_out), .Q(b), .clk(clock));  // open: en, clr
  Register #(.width(32)) register_3 (.D(multiplexer_3_out), .Q(c), .clk(clock));  // open: en, clr
  Register #(.width(32)) register_4 (.D(multiplexer_4_out), .Q(d), .clk(clock));  // open: en, clr
  Register #(.width(32)) register_5 (.D(multiplexer_5_out), .Q(e), .clk(clock));  // open: en, clr
  Register #(.width(32)) register_6 (.D(multiplexer_6_out), .Q(f), .clk(clock));  // open: en, clr
  Register #(.width(32)) register_7 (.D(multiplexer_7_out), .Q(g), .clk(clock));  // open: en, clr
  Register #(.width(32)) register_8 (.D(multiplexer_8_out), .Q(h), .clk(clock));  // open: en, clr
  Multiplexer #(.width(32)) multiplexer_9 (
    .in0(in_1), .in1(shifter_1_out), .out(multiplexer_9_out), .sel(ini));  // open: en
  Register #(.width(32)) register_9 (.D(multiplexer_9_out), .Q(register_9_q), .clk(clock));  // open: en, clr
  matrix_multiply matrix_multiply_1 (
    .in_1(e), .in_2(f), .in_3(g), .in_4(h), .in_5(e), .in_6(f), .in_7(g), .in_8(h), .out_9(ee), .out_10(ff),
    .out_11(gg), .out_12(hh));
  assign and_2_out = 32'h1 & register_9_q;  // AND_Gate and_2, 32 bits wide
  Shifter #(.width(32), .shift("lr")) shifter_1 (.in(register_9_q), .\dist (5'b00001), .out(shifter_1_out));
  Multiplexer #(.width(32)) multiplexer_10 (.in0(a), .in1(aa1), .out(aa), .sel(check));  // open: en
  Multiplexer #(.width(32)) multiplexer_11 (.in0(b), .in1(bb1), .out(bb), .sel(check));  // open: en
  Multiplexer #(.width(32)) multiplexer_12 (.in0(c), .in1(cc1), .out(cc), .sel(check));  // open: en
  Multiplexer #(.width(32)) multiplexer_13 (.in0(d), .in1(dd1), .out(dd), .sel(check));  // open: en
  Comparator #(.width(32), .mode("unsigned")) comparator_3 (.a({32{1'b0}}), .b(and_2_out), .lt(check));  // open: gt, eq
  matrix_multiply matrix_multiply_2 (
    .in_1(a), .in_2(b), .in_3(c), .in_4(d), .in_5(e), .in_6(f), .in_7(g), .in_8(h), .out_9(aa1),
    .out_10(bb1), .out_11(cc1), .out_12(dd1));
  Multiplexer #(.width(32)) multiplexer_14 (.in0({32{1'b0}}), .in1(b), .out(out_2), .sel(tag));  // open: en

  // Other names for the same wires on the sheet: in[31:0] = in_1
endmodule

module matrix_multiply (
  input  [31:0] in_1,
  input  [31:0] in_2,
  input  [31:0] in_3,
  input  [31:0] in_4,
  input  [31:0] in_5,
  input  [31:0] in_6,
  input  [31:0] in_7,
  input  [31:0] in_8,
  output [31:0] out_9,
  output [31:0] out_10,
  output [31:0] out_11,
  output [31:0] out_12
);

  wire [31:0] multiplier_1_out, multiplier_2_out, multiplier_3_out, multiplier_4_out, multiplier_5_out,
       multiplier_6_out, multiplier_7_out, multiplier_8_out;

  Multiplier #(.width(32)) multiplier_1 (.a(in_1), .b(in_5), .out(multiplier_1_out));  // open: cin, cout
  Multiplier #(.width(32)) multiplier_2 (.a(in_2), .b(in_7), .out(multiplier_2_out));  // open: cin, cout
  Multiplier #(.width(32)) multiplier_3 (.a(in_1), .b(in_6), .out(multiplier_3_out));  // open: cin, cout
  Multiplier #(.width(32)) multiplier_4 (.a(in_2), .b(in_8), .out(multiplier_4_out));  // open: cin, cout
  Multiplier #(.width(32)) multiplier_5 (.a(in_3), .b(in_5), .out(multiplier_5_out));  // open: cin, cout
  Multiplier #(.width(32)) multiplier_6 (.a(in_4), .b(in_7), .out(multiplier_6_out));  // open: cin, cout
  Multiplier #(.width(32)) multiplier_7 (.a(in_3), .b(in_6), .out(multiplier_7_out));  // open: cin, cout
  Multiplier #(.width(32)) multiplier_8 (.a(in_4), .b(in_8), .out(multiplier_8_out));  // open: cin, cout
  Adder #(.width(32)) adder_1 (.a(multiplier_1_out), .b(multiplier_2_out), .out(out_9));  // open: cin, cout
  Adder #(.width(32)) adder_2 (.a(multiplier_3_out), .b(multiplier_4_out), .out(out_10));  // open: cin, cout
  Adder #(.width(32)) adder_3 (.a(multiplier_5_out), .b(multiplier_6_out), .out(out_11));  // open: cin, cout
  Adder #(.width(32)) adder_4 (.a(multiplier_7_out), .b(multiplier_8_out), .out(out_12));  // open: cin, cout

  // Other names for the same wires on the sheet: _1_1[31:0] = in_1; _1_2[31:0] = in_2; _1_3[31:0] = in_3;
  //   _1_4[31:0] = in_4; _2_1[31:0] = in_5; _2_2[31:0] = in_6; _2_3[31:0] = in_7; _2_4[31:0] = in_8
endmodule
